# Fritzing sketch ESP8266-Programming-Mode (saved by Fritzing 0.9.10b)

parts:
  U1 = ESP8266 WiFi Module [part_number=ESP8266]
  Part1 = Arduino Uno (Rev3)
  S1 = Pushbutton [package=THT]

nets:
  N1: U1.RXD, Part1.D0/RX
  VCC: U1.VCC, Part1.3V3
  N2: U1.GPIO_16, S1.leg1
  GND: U1.GND, Part1.GND
  N3: U1.TXD, Part1.D1/TX

notes:
  ESP8266 Programming Mode
  GPIO_0 is connected to GND. When uploading a new sketch, press the button to connect RST to GND for 1 second.
  RESET is connected to GND to "disable" the Arduino board, so the program gets uploaded to the ESP8266 module.

custom parts:
  ESP8266 WiFi Module: Generic WiFi Module based on the ESP8266 with onboard PCB antenna and UART communications
